// Logisim project 7seg.circ as structural Verilog: 1 circuit, main circuit 7 segment decoder
module _7_segment_decoder (
);

  wire B_prime_A_prime_out, BA_out, BA_prime_out, button_1_out, button_2_out, button_3_out, button_4_out,
       C_prime_A_prime_out, C_prime_B_out, CA_out, CA_prime_out, CB_prime_A_out, CB_prime_out, not_1_out,
       not_2_out, not_3_out, not_4_out, or_1_out, or_2_out, or_3_out, or_4_out, or_5_out, or_6_out, or_7_out,
       or_8_out, or_9_out, or_10_out, or_11_out, or_12_out, or_13_out, or_14_out, or_15_out, or_16_out,
       or_17_out;

  Button button_1 (.out(button_1_out));
  Button button_2 (.out(button_2_out));
  Button button_3 (.out(button_3_out));
  not not_1 (not_1_out, button_2_out);
  not not_2 (not_2_out, button_3_out);
  not not_3 (not_3_out, button_1_out);
  Button button_4 (.out(button_4_out));
  not not_4 (not_4_out, button_4_out);
  and CB_prime (CB_prime_out, button_2_out, not_2_out);
  and C_prime_A_prime (C_prime_A_prime_out, not_1_out, not_4_out);
  and CA (CA_out, button_2_out, button_4_out);
  and C_prime_B (C_prime_B_out, not_1_out, button_3_out);
  and B_prime_A_prime (B_prime_A_prime_out, not_2_out, not_4_out);
  and BA (BA_out, button_4_out, button_3_out);
  and CB_prime_A (CB_prime_A_out, CB_prime_out, not_4_out);
  and BA_prime (BA_prime_out, button_3_out, not_4_out);
  and CA_prime (CA_prime_out, button_2_out, not_4_out);
  or or_1 (or_1_out, C_prime_B_out, button_1_out);
  or or_2 (or_2_out, B_prime_A_prime_out, BA_out);
  or or_3 (or_3_out, not_2_out, button_4_out);
  or or_4 (or_4_out, CB_prime_A_out, C_prime_A_prime_out);
  or or_5 (or_5_out, C_prime_B_out, BA_prime_out);
  or or_6 (or_6_out, CA_prime_out, button_1_out);
  or or_7 (or_7_out, CB_prime_out, B_prime_A_prime_out);
  or or_8 (or_8_out, C_prime_B_out, CB_prime_out);
  or or_9 (or_9_out, CA_prime_out, button_1_out);
  or or_10 (or_10_out, C_prime_A_prime_out, CA_out);
  or or_11 (or_11_out, or_10_out, or_1_out);
  or or_12 (or_12_out, or_2_out, not_1_out);
  or or_13 (or_13_out, or_3_out, button_2_out);
  or or_14 (or_14_out, or_4_out, or_5_out);
  or or_15 (or_15_out, C_prime_A_prime_out, BA_prime_out);
  or or_16 (or_16_out, or_6_out, or_7_out);
  or or_17 (or_17_out, or_8_out, or_9_out);
  _7_Segment_Display u_7_segment_display_1 (
    .g(or_17_out), .f(or_16_out), .a(or_11_out), .b(or_12_out), .e(or_15_out), .d(or_14_out), .c(or_13_out));  // open: dp

  // Notes on the sheet:
  //   C'
  //   C'A'
  //   C'B
  //   C'A'+CA
  //   C'B + D
  //   B'A' + BA
  //   B'+A
  //   C
  //   CB'A + C'A'
  //   C'B+BA'
  //   CA' + D
  //   B'A+CB'
  //   C'B+CB'
  //   CA'+D
  //   C'A'+BA'
  //   a
  //   b
  //   c
  //   d
  //   e
  //   f
  //   g
endmodule
