// Logisim project 7seg_basicgates.circ as structural Verilog: 1 circuit, main circuit 7segcircuit
module _7segcircuit (
  input  D,
  input  C,
  input  B,
  input  A
);

  wire _7408_2_out, _7408_3_out, _7408_out, _7432_2_out, _7432_3_out, _7432_out, _7486_2_out, _7486_3_out,
       _7486_4_out, _7486_out, and_1_out, and_2_out, and_3_out, and_4_out, and_5_out, and_6_out, and_7_out,
       and_8_out, and_9_out, G_out, not_1_out, NOT_2_out, not_3_out, not_4_out, NOT_5_out, not_7_out,
       not_8_out, not_9_out, not_10_out, not_11_out, not_12_out, NOT_13_out, not_14_out, not_15_out,
       not_16_out, not_17_out, not_18_out, or_1_out, or_2_out, or_3_out, or_4_out, or_5_out, or_6_out,
       or_7_out, or_8_out, or_9_out, or_10_out, or_11_out, or_12_out, or_13_out, undriven, undriven_2,
       undriven_3, undriven_4, undriven_5, undriven_6, undriven_7, undriven_8, undriven_9, undriven_10,
       undriven_11, undriven_12, undriven_13, undriven_14, undriven_15, undriven_16, undriven_17,
       undriven_18, undriven_19, undriven_20, undriven_21, undriven_22, undriven_23, undriven_24,
       undriven_25, undriven_26, undriven_27, undriven_28, undriven_29, undriven_30, undriven_31,
       undriven_32, undriven_33, undriven_34, undriven_35, undriven_36, undriven_37, undriven_38,
       undriven_39, undriven_40, undriven_41, xor_1_out, xor_2_out, xor_3_out;

  not not_1 (not_1_out, xor_1_out);
  xor xor_1 (xor_1_out, C, A);
  xor xor_2 (xor_2_out, A, B);
  not NOT_2 (NOT_2_out, xor_2_out);
  not not_3 (not_3_out, B);
  and _7408 (_7408_out, not_11_out, not_3_out);
  and and_1 (and_1_out, not_11_out, B);
  and _7408_2 (_7408_2_out, undriven, undriven_2);
  not not_4 (not_4_out, undriven_7);
  not NOT_5 (NOT_5_out, C);
  // NOT_Gate not_6 is placed but not wired
  not not_7 (not_7_out, undriven_10);
  xor xor_3 (xor_3_out, not_9_out, xor_1_out);
  xor G (G_out, B, C);
  not not_8 (not_8_out, undriven_9);
  not not_9 (not_9_out, B);
  not not_10 (not_10_out, undriven_8);
  not not_11 (not_11_out, A);
  and and_2 (and_2_out, B, xor_1_out);
  and and_3 (and_3_out, NOT_5_out, not_11_out);
  and and_4 (and_4_out, not_11_out, or_5_out);
  and and_5 (and_5_out, undriven_6, undriven_4);
  and and_6 (and_6_out, undriven_3, undriven_5);
  not not_12 (not_12_out, undriven_11);
  or or_1 (or_1_out, B, not_1_out);
  or or_2 (or_2_out, NOT_5_out, NOT_2_out);
  or _7432 (_7432_out, G_out, and_1_out);
  or or_3 (or_3_out, C, _7408_out);
  or or_4 (or_4_out, D, or_1_out);
  or or_5 (or_5_out, NOT_5_out, B);
  or _7432_2 (_7432_2_out, A, not_3_out);
  or or_6 (or_6_out, xor_3_out, and_2_out);
  or or_7 (or_7_out, D, _7432_out);
  or or_8 (or_8_out, or_3_out, D);
  _7_Segment_Display u_7_segment_display_1 (
    .g(or_7_out), .f(or_8_out), .a(or_4_out), .b(or_2_out), .e(and_4_out), .d(or_10_out), .c(or_9_out));  // open: dp
  or or_9 (or_9_out, C, _7432_2_out);
  or or_10 (or_10_out, or_6_out, and_3_out);
  xor _7486 (_7486_out, undriven_19, undriven_14);
  xor _7486_2 (_7486_2_out, undriven_12, undriven_15);
  and and_7 (and_7_out, undriven_20, undriven_16);
  and _7408_3 (_7408_3_out, undriven_13, undriven_17);
  not NOT_13 (NOT_13_out, undriven_21);
  not not_14 (not_14_out, undriven_26);
  not not_15 (not_15_out, undriven_23);
  not not_16 (not_16_out, undriven_18);
  or or_11 (or_11_out, undriven_22, undriven_25);
  xor _7486_3 (_7486_3_out, undriven_34, undriven_30);
  xor _7486_4 (_7486_4_out, undriven_28, undriven_31);
  and and_8 (and_8_out, undriven_35, undriven_32);
  and and_9 (and_9_out, undriven_29, undriven_33);
  not not_17 (not_17_out, undriven_37);
  not not_18 (not_18_out, undriven_36);
  or _7432_3 (_7432_3_out, undriven_27, undriven_24);
  or or_12 (or_12_out, undriven_41, undriven_39);
  or or_13 (or_13_out, undriven_38, undriven_40);

  // Notes on the sheet:
  //   for d
  //   3rd of F
  //   latter 2 of D
endmodule
