// Logisim project basicgates.circ as structural Verilog: 1 circuit, main circuit 7segcircuit
module _7segcircuit (
  input  D,
  input  C,
  input  B,
  input  A
);

  wire _7408_2_out, _7408_3_out, _7408_out, _7432_out, _7486_2_out, _7486_3_out, _7486_4_out, _7486_5_out,
       _7486_6_out, _7486_7_out, _7486_8_out, _7486_out, and_1_out, and_2_out, and_3_out, and_4_out,
       and_5_out, and_6_out, and_7_out, and_8_out, and_9_out, not_2_out, not_3_out, not_4_out, not_5_out,
       not_6_out, NOT_7_out, not_8_out, not_9_out, not_10_out, not_11_out, not_12_out, NOT_out, or_1_out,
       or_2_out, or_3_out, or_4_out, or_5_out, or_6_out, or_7_out, or_8_out, or_9_out, or_10_out, or_11_out,
       or_12_out, or_13_out, or_14_out, or_15_out, undriven, undriven_2, undriven_3, undriven_4, undriven_5,
       undriven_6, undriven_7, undriven_8, undriven_9, undriven_10, undriven_11, undriven_12, undriven_13,
       undriven_14, undriven_15, undriven_16, undriven_17, undriven_18, undriven_19, undriven_20,
       undriven_21, undriven_22, undriven_23, undriven_24, undriven_25, undriven_26, undriven_27,
       undriven_28, undriven_29, undriven_30, undriven_31, undriven_32, undriven_33, undriven_34,
       undriven_35, undriven_36, undriven_37, undriven_38, undriven_39, undriven_40, undriven_41,
       undriven_42, undriven_43, undriven_44, undriven_45, undriven_46, undriven_47, undriven_48,
       undriven_49, undriven_50, undriven_51, undriven_52, undriven_53, undriven_54, undriven_55,
       undriven_56, undriven_57, undriven_58, undriven_59, undriven_60, undriven_61, undriven_62,
       undriven_63, undriven_64, undriven_65, undriven_66, undriven_67, xor_1_out, xor_2_out, xor_3_out,
       xor_4_out;

  not NOT (NOT_out, A);
  not not_2 (not_2_out, C);
  and and_1 (and_1_out, C, A);
  and _7408 (_7408_out, A, B);
  and and_2 (and_2_out, undriven_4, undriven_2);
  and _7408_2 (_7408_2_out, undriven, undriven_3);
  not not_3 (not_3_out, undriven_11);
  not not_4 (not_4_out, B);
  not not_5 (not_5_out, undriven_5);
  not not_6 (not_6_out, undriven_10);
  and and_3 (and_3_out, NOT_out, not_2_out);
  and and_4 (and_4_out, NOT_out, not_4_out);
  and and_5 (and_5_out, undriven_9, undriven_7);
  and and_6 (and_6_out, undriven_6, undriven_8);
  or _7432 (_7432_out, _7408_out, and_4_out);
  or or_1 (or_1_out, and_1_out, and_3_out);
  xor _7486 (_7486_out, undriven_15, undriven_13);
  xor _7486_2 (_7486_2_out, undriven_12, undriven_14);
  or or_2 (or_2_out, D, B);
  or or_3 (or_3_out, or_1_out, or_2_out);
  or or_4 (or_4_out, _7432_out, not_2_out);
  or or_5 (or_5_out, A, C);
  or or_6 (or_6_out, or_5_out, not_4_out);
  xor _7486_3 (_7486_3_out, undriven_22, undriven_18);
  xor _7486_4 (_7486_4_out, undriven_16, undriven_19);
  or or_7 (or_7_out, undriven_23, undriven_20);
  or or_8 (or_8_out, undriven_17, undriven_21);
  _7_Segment_Display u_7_segment_display_1 (.a(or_3_out), .b(or_4_out), .c(or_6_out));  // open: g, f, e, d, dp
  or or_9 (or_9_out, undriven_25, undriven_24);
  or or_10 (or_10_out, undriven_29, undriven_27);
  or or_11 (or_11_out, undriven_26, undriven_28);
  xor _7486_5 (_7486_5_out, undriven_34, undriven_31);
  xor _7486_6 (_7486_6_out, undriven_30, undriven_32);
  and and_7 (and_7_out, undriven_37, undriven_35);
  and _7408_3 (_7408_3_out, undriven_33, undriven_36);
  or or_12 (or_12_out, undriven_40, undriven_47);
  xor _7486_7 (_7486_7_out, undriven_48, undriven_41);
  xor _7486_8 (_7486_8_out, undriven_38, undriven_42);
  and and_8 (and_8_out, undriven_53, undriven_49);
  and and_9 (and_9_out, undriven_43, undriven_50);
  not NOT_7 (NOT_7_out, undriven_55);
  not not_8 (not_8_out, undriven_59);
  not not_9 (not_9_out, undriven_56);
  not not_10 (not_10_out, undriven_54);
  xor xor_1 (xor_1_out, undriven_51, undriven_44);
  xor xor_2 (xor_2_out, undriven_57, undriven_61);
  xor xor_3 (xor_3_out, undriven_39, undriven_45);
  or or_13 (or_13_out, undriven_52, undriven_46);
  or or_14 (or_14_out, undriven_65, undriven_62);
  or or_15 (or_15_out, undriven_58, undriven_63);
  not not_11 (not_11_out, undriven_67);
  not not_12 (not_12_out, undriven_66);
  xor xor_4 (xor_4_out, undriven_64, undriven_60);
endmodule
