// Logisim project 7seg_mod.circ as structural Verilog: 1 circuit, main circuit 7 segment decoder
module _7_segment_decoder (
  input  D,
  input  C,
  input  B,
  input  A
);

  wire and_1_out, and_2_out, B_prime_A_prime_out, BA_out, BA_prime_out, C_prime_A_prime_out, C_prime_B_out,
       CA_out, CA_prime_out, CB_prime_A_out, CB_prime_out, not_1_out, not_2_out, not_3_out, not_4_out,
       or_1_out, or_2_out, or_3_out, or_4_out, or_5_out, or_6_out, or_7_out, or_8_out, or_9_out, or_10_out,
       or_11_out, or_12_out, or_13_out, or_14_out, or_15_out, or_16_out, or_17_out, or_18_out, or_19_out;

  not not_1 (not_1_out, C);
  not not_2 (not_2_out, B);
  not not_3 (not_3_out, D);
  not not_4 (not_4_out, A);
  and CB_prime (CB_prime_out, C, not_2_out);
  and and_1 (and_1_out, C, A);
  and and_2 (and_2_out, not_1_out, not_4_out);
  and C_prime_A_prime (C_prime_A_prime_out, not_1_out, not_4_out);
  and CA (CA_out, C, A);
  and C_prime_B (C_prime_B_out, not_1_out, B);
  and B_prime_A_prime (B_prime_A_prime_out, not_2_out, not_4_out);
  and BA (BA_out, A, B);
  and CB_prime_A (CB_prime_A_out, CB_prime_out, A);
  and BA_prime (BA_prime_out, B, not_4_out);
  and CA_prime (CA_prime_out, C, not_4_out);
  or or_1 (or_1_out, and_1_out, and_2_out);
  or or_2 (or_2_out, B, D);
  or or_3 (or_3_out, C_prime_B_out, D);
  or or_4 (or_4_out, B_prime_A_prime_out, BA_out);
  or or_5 (or_5_out, not_2_out, A);
  or or_6 (or_6_out, CB_prime_A_out, C_prime_A_prime_out);
  or or_7 (or_7_out, C_prime_B_out, BA_prime_out);
  or or_8 (or_8_out, CA_prime_out, D);
  or or_9 (or_9_out, CB_prime_out, B_prime_A_prime_out);
  or or_10 (or_10_out, C_prime_B_out, CB_prime_out);
  or or_11 (or_11_out, CA_prime_out, D);
  or or_12 (or_12_out, C_prime_A_prime_out, CA_out);
  or or_13 (or_13_out, or_1_out, or_2_out);
  or or_14 (or_14_out, or_4_out, not_1_out);
  or or_15 (or_15_out, or_5_out, C);
  or or_16 (or_16_out, or_6_out, or_7_out);
  or or_17 (or_17_out, C_prime_A_prime_out, BA_prime_out);
  or or_18 (or_18_out, or_8_out, or_9_out);
  or or_19 (or_19_out, or_10_out, or_11_out);
  _7_Segment_Display u_7_segment_display_1 (
    .g(or_19_out), .f(or_18_out), .a(or_13_out), .b(or_14_out), .e(or_17_out), .d(or_16_out), .c(or_15_out));  // open: dp

  // Notes on the sheet:
  //   XNOR equivalent
  //   C'
  //   C'A'
  //   C'B
  //   C'A'+CA
  //   C'B + D
  //   B'A' + BA
  //   B'+A
  //   C
  //   CB'A + C'A'
  //   C'B+BA'
  //   CA' + D
  //   B'A+CB'
  //   C'B+CB'
  //   CA'+D
  //   C'A'+BA'
  //   a
  //   b
  //   c
  //   d
  //   e
  //   f
  //   g
endmodule
